// Logisim project alu.circ as structural Verilog: 13 circuits, main circuit alu
module alu (
  input  [31:0] A,
  input  [31:0] B,
  input  [3:0] ALUSel,
  output [31:0] Result
);

  wire comparator_1_lt, comparator_2_eq;
  wire [31:0] add_3, adder_1_out, and_0, bit_extender_2_out, bit_extender_3_out, cnto_15,
       count_1s_32bit_1_result, count_1s_32bit_2_result, div_9, divu_8, mulh_7, mulhu_6, mult_5,
       multiplier_1_out, multiplier_2_cout, multiplier_3_out, or_1, remu_10, sir_14, sll14, slt_13, sra_12,
       srl_11, sub_4, undriven, xor_2;

  Shifter #(.width(32)) shifter_1 (.in(A), .\dist (B[4:0]), .out(sll14));
  Divider #(.width(32)) divider_1 (.a(A), .b(B), .out(divu_8));  // open: upper, rem
  Comparator #(.width(32)) comparator_1 (.a(A), .b(B), .lt(comparator_1_lt));  // open: gt, eq
  assign slt_13 = {{31{1'b0}}, comparator_1_lt};  // Bit_Extender bit_extender_1
  assign and_0 = A & B;  // AND_Gate and_1, 32 bits wide
  Subtractor #(.width(32)) subtractor_1 (.a(A), .b(B), .out(sub_4));  // open: bin, bout
  assign bit_extender_2_out = {{31{A[31]}}, A[31]};  // Bit_Extender bit_extender_2
  assign bit_extender_3_out = {{31{B[31]}}, B[31]};  // Bit_Extender bit_extender_3
  Multiplier #(.width(32)) multiplier_1 (.a(bit_extender_2_out), .b(B), .out(multiplier_1_out));  // open: cin, cout
  Multiplier #(.width(32)) multiplier_2 (.a(A), .b(B), .cout(multiplier_2_cout));  // open: out, cin
  Multiplier #(.width(32)) multiplier_3 (.a(A), .b(bit_extender_3_out), .out(multiplier_3_out));  // open: cin, cout
  assign or_1 = A | B;  // OR_Gate or_1, 32 bits wide
  Multiplier #(.width(32)) multiplier_4 (.a(A), .b(B), .out(mult_5));  // open: cin, cout
  signedDivision signeddivision_1 (.A(A), .B(B), .ANS(div_9));
  Adder #(.width(32)) adder_1 (.a(multiplier_1_out), .b(multiplier_3_out), .out(adder_1_out));  // open: cin, cout
  Comparator #(.width(32)) comparator_2 (
    .a(A),
    .b({B[0], B[1], B[2], B[3], B[4], B[5], B[6], B[7], B[8], B[9], B[10], B[11], B[12], B[13], B[14], B[15], B[16], B[17], B[18], B[19], B[20], B[21], B[22], B[23], B[24], B[25], B[26], B[27], B[28], B[29], B[30], B[31]}),
    .eq(comparator_2_eq));  // open: gt, lt
  assign sir_14 = {{31{1'b0}}, comparator_2_eq};  // Bit_Extender bit_extender_4
  Adder #(.width(32)) adder_2 (.a(multiplier_2_cout), .b(adder_1_out), .out(mulh_7));  // open: cin, cout
  Multiplexer #(.select(4), .width(32), .enable("false")) multiplexer_1 (
    .in0(add_3), .in1(or_1), .in2(xor_2), .in3(and_0), .in4(sub_4), .in5(mult_5), .in6(mulhu_6),
    .in7(mulh_7), .in8(divu_8), .in9(div_9), .in10(remu_10), .in11(srl_11), .in12(sra_12), .in13(slt_13),
    .in14(sll14), .in15(undriven), .out(Result), .sel(ALUSel));
  assign xor_2 = A ^ B;  // XOR_Gate xor_1, 32 bits wide
  Multiplier #(.width(32)) multiplier_5 (.a(A), .b(B), .cout(mulhu_6));  // open: out, cin
  Divider #(.width(32)) divider_2 (.a(A), .b(B), .rem(remu_10));  // open: out, upper
  Shifter #(.width(32), .shift("ar")) shifter_2 (.in(A), .\dist (B[4:0]), .out(sra_12));
  Adder #(.width(32)) adder_3 (.a(A), .b(B), .out(add_3));  // open: cin, cout
  Shifter #(.width(32), .shift("lr")) shifter_3 (.in(A), .\dist (B[4:0]), .out(srl_11));
  count_1s_32bit count_1s_32bit_1 (.param(A), .result(count_1s_32bit_1_result));
  count_1s_32bit count_1s_32bit_2 (.param(B), .result(count_1s_32bit_2_result));
  Adder #(.width(32)) adder_4 (
    .a(count_1s_32bit_1_result), .b(count_1s_32bit_2_result), .out(cnto_15));  // open: cin, cout

  // Notes on the sheet:
  //   INPUTS to your circuit
  //   DON'T CHANGE THE LOCATIONS OF THE INPUTS AND OUTPUTS!
  //   OUTPUT from your circuit
  //   only need low 5 bits of B
endmodule

module test (
  input  [31:0] in_1,
  input  [31:0] in_2,
  input  [3:0] in_3,
  output [31:0] out_4
);

  count_1s_32bit count_1s_32bit_1 (.result(in_1));  // open: param

  // Other names for the same wires on the sheet: A[31:0] = in_1; ALUSel[3:0] = in_3; B[31:0] = in_2;
  //   result[31:0] = out_4

  // Notes on the sheet:
  //   INPUTS to your circuit
  //   OUTPUT from your circuit
endmodule

module count_1s_32bit (
  input  [31:0] param,
  output [31:0] result
);

  wire [31:0] count_1s_16bit_1_result, count_1s_16bit_2_result;

  count_1s_16bit count_1s_16bit_1 (.param(param[15:0]), .result(count_1s_16bit_1_result));
  count_1s_16bit count_1s_16bit_2 (.param(param[31:16]), .result(count_1s_16bit_2_result));
  Adder #(.width(32)) adder_1 (
    .a(count_1s_16bit_1_result), .b(count_1s_16bit_2_result), .out(result));  // open: cin, cout
endmodule

module count_1s_16bit (
  input  [15:0] param,
  output [31:0] result
);

  wire [31:0] count_1s_8bit_1_result, count_1s_8bit_2_result;

  count_1s_8bit count_1s_8bit_1 (.param(param[7:0]), .result(count_1s_8bit_1_result));
  count_1s_8bit count_1s_8bit_2 (.param(param[15:8]), .result(count_1s_8bit_2_result));
  Adder #(.width(32)) adder_1 (
    .a(count_1s_8bit_1_result), .b(count_1s_8bit_2_result), .out(result));  // open: cin, cout
endmodule

module count_1s_8bit (
  input  [7:0] param,
  output [31:0] result
);

  wire [31:0] count_1s_4bit_1_result, count_1s_4bit_2_result;

  count_1s_4bit count_1s_4bit_1 (.param(param[3:0]), .result(count_1s_4bit_1_result));
  count_1s_4bit count_1s_4bit_2 (.param(param[7:4]), .result(count_1s_4bit_2_result));
  Adder #(.width(32)) adder_1 (
    .a(count_1s_4bit_1_result), .b(count_1s_4bit_2_result), .out(result));  // open: cin, cout
endmodule

module count_1s_4bit (
  input  [3:0] param,
  output [31:0] result
);

  wire [31:0] count_1s_2bit_1_ans, count_1s_2bit_2_ans;

  count_1s_2bit count_1s_2bit_1 (.param(param[1:0]), .ans(count_1s_2bit_1_ans));
  count_1s_2bit count_1s_2bit_2 (.param(param[3:2]), .ans(count_1s_2bit_2_ans));
  Adder #(.width(32)) adder_1 (.a(count_1s_2bit_1_ans), .b(count_1s_2bit_2_ans), .out(result));  // open: cin, cout
endmodule

module count_1s_2bit (
  input  [1:0] param,
  output [31:0] ans
);

  wire [31:0] bit_extender_1_out, bit_extender_2_out;

  // Probe on param[0]
  // Probe on param[1]
  // Probe on bit_extender_1_out
  assign bit_extender_1_out = {{31{1'b0}}, param[0]};  // Bit_Extender bit_extender_1
  assign bit_extender_2_out = {{31{1'b0}}, param[1]};  // Bit_Extender bit_extender_2
  // Probe on bit_extender_2_out
  Adder #(.width(32)) adder_1 (.a(bit_extender_1_out), .b(bit_extender_2_out), .out(ans));  // open: cin, cout
endmodule

module signedDivision (
  input  [31:0] A,
  input  [31:0] B,
  output [31:0] ANS
);

  wire NegativeOrNot_out;
  wire [31:0] adder_1_out, divider_1_out, multiplexer_1_out, multiplexer_2_out, negateallbit_1_answer,
       negateallbit_2_answer, negateallbit_3_answer, subtractor_1_out, subtractor_2_out;

  // Probe on B
  // Probe on A
  // Probe on A
  // Probe on B
  Subtractor #(.width(32)) subtractor_1 (.a(B), .b(32'h1), .out(subtractor_1_out));  // open: bin, bout
  // Probe on ANS
  // Probe on subtractor_2_out
  Subtractor #(.width(32)) subtractor_2 (.a(A), .b(32'h1), .out(subtractor_2_out));  // open: bin, bout
  negateAllBit negateallbit_1 (.param(subtractor_1_out), .answer(negateallbit_1_answer));
  // Probe on negateallbit_2_answer
  negateAllBit negateallbit_2 (.param(subtractor_2_out), .answer(negateallbit_2_answer));
  Multiplexer #(.width(32), .enable("false")) multiplexer_1 (
    .in0(B), .in1(negateallbit_1_answer), .out(multiplexer_1_out), .sel(B[31]));
  // Probe on negateallbit_1_answer
  Multiplexer #(.width(32), .enable("false")) multiplexer_2 (
    .in0(A), .in1(negateallbit_2_answer), .out(multiplexer_2_out), .sel(A[31]));
  // Probe on divider_1_out
  Divider #(.width(32)) divider_1 (
    .a(multiplexer_2_out), .b(multiplexer_1_out), .out(divider_1_out));  // open: upper, rem
  // Probe on NegativeOrNot_out
  xor NegativeOrNot (NegativeOrNot_out, A[31], B[31]);
  negateAllBit negateallbit_3 (.param(divider_1_out), .answer(negateallbit_3_answer));
  Adder #(.width(32)) adder_1 (.a(negateallbit_3_answer), .b(32'h1), .out(adder_1_out));  // open: cin, cout
  // Probe on ANS
  Multiplexer #(.width(32), .enable("false")) multiplexer_3 (
    .in0(divider_1_out), .in1(adder_1_out), .out(ANS), .sel(NegativeOrNot_out));

  // Other names for the same wires on the sheet: A_35459d1a[31:0] = A; ANS_f1395645[31:0] = ANS; B_7a30659a[31:0] = B
endmodule

module negateAllBit (
  input  [31:0] param,
  output [31:0] answer
);

  not not_1 (answer[0], param[0]);
  not not_2 (answer[1], param[1]);
  not not_3 (answer[2], param[2]);
  not not_4 (answer[9], param[9]);
  not not_5 (answer[10], param[10]);
  not not_6 (answer[11], param[11]);
  not not_7 (answer[12], param[12]);
  not not_8 (answer[13], param[13]);
  not not_9 (answer[14], param[14]);
  not not_10 (answer[21], param[21]);
  not not_11 (answer[22], param[22]);
  not not_12 (answer[23], param[23]);
  not not_13 (answer[24], param[24]);
  not not_14 (answer[25], param[25]);
  not not_15 (answer[30], param[30]);
  not not_16 (answer[31], param[31]);
  not not_17 (answer[3], param[3]);
  not not_18 (answer[4], param[4]);
  not not_19 (answer[6], param[6]);
  not not_20 (answer[7], param[7]);
  not not_21 (answer[8], param[8]);
  not not_22 (answer[15], param[15]);
  not not_23 (answer[16], param[16]);
  not not_24 (answer[17], param[17]);
  not not_25 (answer[18], param[18]);
  not not_26 (answer[19], param[19]);
  not not_27 (answer[20], param[20]);
  not not_28 (answer[26], param[26]);
  not not_29 (answer[27], param[27]);
  not not_30 (answer[28], param[28]);
  not not_31 (answer[29], param[29]);
  not not_32 (answer[5], param[5]);

  // Notes on the sheet:
  //   reverse all bits of a 32 bit number by hand
endmodule

module signedMulHighBits (
  input  [31:0] input1,
  input  [31:0] input2,
  output [31:0] output1
);

  wire mathmeticalmultiplication_1_positive;
  wire [31:0] mathmeticalmultiplication_1_highbits, p2n_1_ans;

  // Probe on input2
  // Probe on input1
  MathmeticalMultiplication mathmeticalmultiplication_1 (
    .A(input1), .B(input2), .highBits(mathmeticalmultiplication_1_highbits),
    .positive(mathmeticalmultiplication_1_positive));  // open: lowBits
  // Probe on output1
  P2N p2n_1 (.param(mathmeticalmultiplication_1_highbits), .ans(p2n_1_ans));
  Multiplexer #(.width(32), .enable("false")) multiplexer_1 (
    .in0(p2n_1_ans), .in1(mathmeticalmultiplication_1_highbits), .out(output1),
    .sel(mathmeticalmultiplication_1_positive));

  // Other names for the same wires on the sheet: A[31:0] = input1; ANS[31:0] = output1; B[31:0] = input2
endmodule

module N2P (
  input  [31:0] param,
  output [31:0] ans
);

  wire [31:0] negateallbit_1_answer;

  // Probe on param
  negateAllBit negateallbit_1 (.param(param), .answer(negateallbit_1_answer));
  Adder #(.width(32)) adder_1 (.a(negateallbit_1_answer), .b(32'h1), .out(ans));  // open: cin, cout
  // Probe on ans

  // Notes on the sheet:
  //   negative to positive 
  //   public static int N2P(int pararm){
  //   return ans;}
  //   int ans = Math.abs(pararm)
  //   if(pararm>=0) throw new RuntimeException("pararm should be negative")
endmodule

module MathmeticalMultiplication (
  input  [31:0] A,
  input  [31:0] B,
  output [31:0] lowBits,
  output [31:0] highBits,
  output positive
);

  wire xor_1_out;
  wire [31:0] multiplexer_1_out, multiplexer_2_out, n2p_1_ans, n2p_2_ans;

  // Probe on A
  // Probe on B
  xor xor_1 (xor_1_out, B[31], A[31]);
  not not_1 (positive, xor_1_out);
  N2P n2p_1 (.param(A), .ans(n2p_1_ans));
  N2P n2p_2 (.param(B), .ans(n2p_2_ans));
  Multiplexer #(.width(32), .enable("false")) multiplexer_1 (
    .in0(A), .in1(n2p_1_ans), .out(multiplexer_1_out), .sel(A[31]));
  Multiplexer #(.width(32), .enable("false")) multiplexer_2 (
    .in0(B), .in1(n2p_2_ans), .out(multiplexer_2_out), .sel(B[31]));
  // Probe on multiplexer_1_out
  // Probe on multiplexer_2_out
  // Probe on lowBits
  Multiplier #(.width(32)) multiplier_1 (
    .a(multiplexer_1_out), .b(multiplexer_2_out), .out(lowBits), .cout(highBits));  // open: cin
  // Probe on highBits
endmodule

module P2N (
  input  [31:0] param,
  output [31:0] ans
);

  wire [31:0] subtractor_1_out;

  // Probe on param
  Subtractor #(.width(32)) subtractor_1 (.a(param), .b(32'h1), .out(subtractor_1_out));  // open: bin, bout
  negateAllBit negateallbit_1 (.param(subtractor_1_out), .answer(ans));
  // Probe on ans

  // Notes on the sheet:
  //    positive to negative
endmodule
