// Logisim project cpu.circ as structural Verilog: 2 circuits, main circuit main
module main (
  input  [31:0] INSTRUCTION,
  input  CLOCK,
  output [31:0] FETCH_ADDRESS,
  output [31:0] ra,
  output [31:0] sp,
  output [31:0] t0,
  output [31:0] t1,
  output [31:0] t2,
  output [31:0] s0,
  output [31:0] s1,
  output [31:0] a0
);

  wire BrEq, BrLt, BrUn, BSel, comparator_1_eq, comparator_1_lt, comparator_2_eq, comparator_2_lt, MemRW,
       PCSel, RegWEn;
  wire [1:0] ASel, WBSel;
  wire [2:0] DataSel, ImmSel;
  wire [3:0] ALUSel;
  wire [31:0] adder_1_out, alu_result, bit_extender_1_out, bit_extender_2_out, bit_extender_3_out,
       bit_extender_4_out, bit_extender_5_out, bit_extender_6_out, bit_extender_7_out, bit_extender_8_out,
       DMEM_readdata, imm, INST, mem_data, multiplexer_1_out, multiplexer_2_out, multiplexer_8_out,
       multiplexer_9_out, pc1, pc2, pc3, r1, r2, wd;

  Adder #(.width(32)) adder_1 (.a(pc1), .b(32'h4), .out(adder_1_out));  // open: cin, cout
  Register #(.width(32)) register_1 (.D(pc1), .clk(CLOCK), .Q(pc2));  // open: en, clr
  Multiplexer #(.width(32), .enable("false")) multiplexer_1 (
    .in0(adder_1_out), .in1(alu_result), .out(multiplexer_1_out), .sel(PCSel));
  Multiplexer #(.width(32), .enable("false")) multiplexer_2 (
    .in0(INSTRUCTION), .in1(32'h13), .out(multiplexer_2_out), .sel(PCSel));
  Multiplexer #(.select(2), .width(32), .enable("false")) multiplexer_3 (
    .in0(mem_data), .in1(alu_result), .in2(pc3), .out(wd), .sel(WBSel));  // open: in3
  Register #(.width(32)) register_2 (.D(multiplexer_1_out), .clk(CLOCK), .Q(pc1));  // open: en, clr
  Register #(.width(32)) register_3 (.D(multiplexer_2_out), .clk(CLOCK), .Q(INST));  // open: en, clr
  Shifter #(.width(32), .shift("lr")) shifter_1 (.in(pc1), .\dist (5'b00010), .out(FETCH_ADDRESS));
  mem_main DMEM (.WriteAddr(alu_result), .WriteData(r2), .MemRW(MemRW), .ReadData(DMEM_readdata), .clk(CLOCK));
  assign bit_extender_1_out = {{24{DMEM_readdata[7]}}, DMEM_readdata[7:0]};  // Bit_Extender bit_extender_1
  assign bit_extender_2_out = {{16{DMEM_readdata[15]}}, DMEM_readdata[15:0]};  // Bit_Extender bit_extender_2
  assign bit_extender_3_out = {{24{1'b0}}, DMEM_readdata[7:0]};  // Bit_Extender bit_extender_3
  assign bit_extender_4_out = {{16{1'b0}}, DMEM_readdata[15:0]};  // Bit_Extender bit_extender_4
  Adder #(.width(32)) adder_2 (.a(pc2), .b(32'h4), .out(pc3));  // open: cin, cout
  Multiplexer #(.select(3), .width(32), .enable("false")) multiplexer_4 (
    .in0(bit_extender_1_out), .in1(bit_extender_2_out), .in2(DMEM_readdata), .in3(bit_extender_3_out),
    .in4(bit_extender_4_out), .out(mem_data), .sel(DataSel));  // open: in5, in6, in7
  assign bit_extender_5_out = {{20{INST[31]}}, INST[31:20]};  // Bit_Extender bit_extender_5
  assign bit_extender_6_out = {{20{INST[31]}}, {INST[31:25], INST[11:7]}};  // Bit_Extender bit_extender_6
  assign bit_extender_7_out = {{19{INST[31]}}, {INST[31], INST[7], INST[30:25], INST[11:8], 1'b0}};  // Bit_Extender bit_extender_7
  assign bit_extender_8_out = {{11{INST[31]}}, {INST[31], INST[19:12], INST[20], INST[30:21], 1'b0}};  // Bit_Extender bit_extender_8
  Comparator #(.width(32)) comparator_1 (.a(r1), .b(r2), .eq(comparator_1_eq), .lt(comparator_1_lt));  // open: gt
  Comparator #(.width(32), .mode("unsigned")) comparator_2 (
    .a(r1), .b(r2), .eq(comparator_2_eq), .lt(comparator_2_lt));  // open: gt
  Multiplexer #(.select(3), .width(32), .enable("false")) multiplexer_5 (
    .in0(bit_extender_5_out), .in1(bit_extender_6_out), .in2(bit_extender_7_out),
    .in3({INST[31:12], {12{1'b0}}}), .in4(bit_extender_8_out), .out(imm), .sel(ImmSel));  // open: in5, in6, in7
  Multiplexer #(.enable("false")) multiplexer_6 (.in0(comparator_1_eq), .in1(comparator_2_eq), .out(BrEq), .sel(BrUn));
  Multiplexer #(.enable("false")) multiplexer_7 (.in0(comparator_1_lt), .in1(comparator_2_lt), .out(BrLt), .sel(BrUn));
  controllogic controllogic_1 (
    .BrEq(BrEq), .in_2(INST), .BrLt(BrLt), .DataSel(DataSel), .ALUSel(ALUSel), .BrUn(BrUn), .MemRW(MemRW),
    .PCSel(PCSel), .ASel(ASel), .BSel(BSel), .ImmSel(ImmSel), .RegWEn(RegWEn), .WBSel(WBSel));
  regfile_main RegFile (
    .rs2(INST[24:20]), .rd(INST[11:7]), .Read_Data_1(r1), .Read_Data_2(r2), .ra(ra), .sp(sp), .t0(t0),
    .t1(t1), .t2(t2), .s0(s0), .s1(s1), .a0(a0), .rs1(INST[19:15]), .Write_Data(wd), .RegWEn(RegWEn),
    .clk(CLOCK));
  Multiplexer #(.select(2), .width(32), .enable("false")) multiplexer_8 (
    .in0(r1), .in1(pc2), .in2({32{1'b0}}), .out(multiplexer_8_out), .sel(ASel));  // open: in3
  Multiplexer #(.width(32), .enable("false")) multiplexer_9 (.in0(r2), .in1(imm), .out(multiplexer_9_out), .sel(BSel));
  alu alu_1 (.A(multiplexer_8_out), .B(multiplexer_9_out), .ALUSel(ALUSel), .Result(alu_result));

  // Other names for the same wires on the sheet: rd[4:0] = INST[11:7]; rs2[4:0] = INST[24:20]; rs1[4:0] = INST[19:15];
  //   clk = CLOCK; fetch_addr[31:0] = FETCH_ADDRESS

  // Notes on the sheet:
  //   Output
  //   Inputs/Outputs from run.circ. DO NOT MOVE THESE.
  //   immI
  //   immS
  //   immB
  //   immU
  //   immJ
  //   Inputs
  //   It is OK to move the PC, RegFile, ALU, and MEM to wherever is most convenient for you when constructing your CPU, and to delete this text
  //   Inputs/Outputs from run.circ. DO NOT MOVE THESE.
endmodule

module controllogic (
  input  BrEq,
  input  [31:0] in_2,
  input  BrLt,
  output [2:0] DataSel,
  output [3:0] ALUSel,
  output BrUn,
  output MemRW,
  output PCSel,
  output [1:0] ASel,
  output BSel,
  output [2:0] ImmSel,
  output RegWEn,
  output [1:0] WBSel
);

  wire add0, and3, and_1_out, and_2_out, and_3_out, and_4_out, and_5_out, and_6_out, comparator_7_eq,
       comparator_8_eq, comparator_9_eq, comparator_10_eq, comparator_13_eq, comparator_15_eq,
       comparator_16_eq, comparator_17_eq, comparator_18_eq, comparator_19_eq, comparator_20_eq,
       comparator_21_eq, comparator_22_eq, comparator_23_eq, comparator_24_eq, comparator_25_eq,
       comparator_26_eq, comparator_27_eq, comparator_28_eq, comparator_29_eq, comparator_30_eq,
       comparator_31_eq, comparator_32_eq, comparator_33_eq, comparator_34_eq, comparator_35_eq,
       comparator_36_eq, comparator_37_eq, comparator_38_eq, comparator_39_eq, comparator_40_eq,
       comparator_41_eq, comparator_42_eq, comparator_43_eq, comparator_44_eq, comparator_45_eq,
       comparator_46_eq, comparator_47_eq, comparator_48_eq, comparator_49_eq, div9, divu8, itype1, itype2,
       itype3, mulh7, mulhu6, mult5, not_1_out, not_2_out, or1, or_1_out, or_2_out, or_3_out, or_4_out,
       or_5_out, or_6_out, or_7_out, or_10_out, remu10, rtype, sbtype, sll14, slt13, sra12, srl11, sub4,
       ujtype, utype1, utype2, xor2;
  wire [1:0] multiplexer_3_out, multiplexer_7_out;
  wire [2:0] f3, multiplexer_22_out, multiplexer_23_out, multiplexer_24_out, multiplexer_25_out,
       multiplexer_27_out, multiplexer_28_out, multiplexer_29_out, multiplexer_30_out;
  wire [3:0] multiplexer_1_out, multiplexer_2_out, multiplexer_4_out, multiplexer_5_out, multiplexer_9_out,
       multiplexer_10_out, multiplexer_11_out, multiplexer_13_out, multiplexer_14_out, multiplexer_15_out,
       multiplexer_16_out, multiplexer_17_out, multiplexer_18_out, multiplexer_20_out;
  wire [6:0] f7;

  Multiplexer #(.width(4), .enable("false")) multiplexer_1 (
    .in0(4'b0000), .in1(4'b0001), .out(multiplexer_1_out), .sel(or1));
  Multiplexer #(.width(4), .enable("false")) multiplexer_2 (
    .in0(multiplexer_1_out), .in1(4'b0010), .out(multiplexer_2_out), .sel(xor2));
  Comparator #(.width(7), .mode("unsigned")) comparator_1 (.a(in_2[6:0]), .b(7'b0110011), .eq(rtype));  // open: gt, lt
  Comparator #(.width(7), .mode("unsigned")) comparator_2 (.a(in_2[6:0]), .b(7'b0000011), .eq(itype1));  // open: gt, lt
  Comparator #(.width(7), .mode("unsigned")) comparator_3 (.a(in_2[6:0]), .b(7'b0100011), .eq(MemRW));  // open: gt, lt
  Comparator #(.width(7), .mode("unsigned")) comparator_4 (.a(in_2[6:0]), .b(7'b1100011), .eq(sbtype));  // open: gt, lt
  Comparator #(.width(7), .mode("unsigned")) comparator_5 (.a(in_2[6:0]), .b(7'b1101111), .eq(ujtype));  // open: gt, lt
  Comparator #(.width(7), .mode("unsigned")) comparator_6 (.a(in_2[6:0]), .b(7'b0010111), .eq(utype1));  // open: gt, lt
  Multiplexer #(.width(2), .enable("false")) multiplexer_3 (
    .in0(2'b00), .in1(2'b01), .out(multiplexer_3_out), .sel(or_1_out));
  or or_1 (or_1_out, ujtype, sbtype, utype1);
  Multiplexer #(.width(4), .enable("false")) multiplexer_4 (
    .in0(multiplexer_2_out), .in1(4'b0011), .out(multiplexer_4_out), .sel(and3));
  or or_2 (or_2_out, ujtype, itype3);
  Comparator #(.width(3), .mode("unsigned")) comparator_7 (
    .a(in_2[14:12]), .b(3'b001), .eq(comparator_7_eq));  // open: gt, lt
  Multiplexer #(.width(4), .enable("false")) multiplexer_5 (
    .in0(multiplexer_4_out), .in1(4'b0100), .out(multiplexer_5_out), .sel(sub4));
  Multiplexer #(.width(2), .enable("false")) multiplexer_6 (
    .in0(multiplexer_3_out), .in1(2'b10), .out(ASel), .sel(utype2));
  Multiplexer #(.width(2), .enable("false")) multiplexer_7 (
    .in0(2'b01), .in1(2'b00), .out(multiplexer_7_out), .sel(itype1));
  Comparator #(.width(3), .mode("unsigned")) comparator_8 (
    .a(in_2[14:12]), .b(3'b100), .eq(comparator_8_eq));  // open: gt, lt
  Comparator #(.width(3), .mode("unsigned")) comparator_9 (
    .a(in_2[14:12]), .b(3'b110), .eq(comparator_9_eq));  // open: gt, lt
  Comparator #(.width(3), .mode("unsigned")) comparator_10 (
    .a(in_2[14:12]), .b(3'b111), .eq(comparator_10_eq));  // open: gt, lt
  Multiplexer #(.width(7), .enable("false")) multiplexer_8 (.in0({7{1'b0}}), .in1(in_2[31:25]), .out(f7), .sel(rtype));
  Multiplexer #(.width(4), .enable("false")) multiplexer_9 (
    .in0(multiplexer_5_out), .in1(4'b0101), .out(multiplexer_9_out), .sel(mult5));
  Multiplexer #(.width(4), .enable("false")) multiplexer_10 (
    .in0(multiplexer_9_out), .in1(4'b0110), .out(multiplexer_10_out), .sel(mulhu6));
  Comparator #(.width(7), .mode("unsigned")) comparator_11 (
    .a(in_2[6:0]), .b(7'b0010011), .eq(itype2));  // open: gt, lt
  Comparator #(.width(7), .mode("unsigned")) comparator_12 (
    .a(in_2[6:0]), .b(7'b0110111), .eq(utype2));  // open: gt, lt
  Comparator #(.width(3), .mode("unsigned")) comparator_13 (
    .a(in_2[14:12]), .b(3'b000), .eq(comparator_13_eq));  // open: gt, lt
  and and_1 (and_1_out, BrLt, comparator_9_eq);
  not not_1 (not_1_out, BrEq);
  and and_2 (and_2_out, not_1_out, comparator_7_eq);
  Multiplexer #(.width(4), .enable("false")) multiplexer_11 (
    .in0(multiplexer_10_out), .in1(4'b0111), .out(multiplexer_11_out), .sel(mulh7));
  Multiplexer #(.width(2), .enable("false")) multiplexer_12 (
    .in0(multiplexer_7_out), .in1(2'b10), .out(WBSel), .sel(or_2_out));
  and and_3 (and_3_out, BrEq, comparator_13_eq);
  and and_4 (and_4_out, comparator_8_eq, BrLt);
  not not_2 (not_2_out, BrLt);
  Multiplexer #(.width(4), .enable("false")) multiplexer_13 (
    .in0(multiplexer_11_out), .in1(4'b1000), .out(multiplexer_13_out), .sel(divu8));
  not not_3 (BSel, rtype);
  and and_5 (and_5_out, comparator_10_eq, not_2_out);
  Multiplexer #(.width(4), .enable("false")) multiplexer_14 (
    .in0(multiplexer_13_out), .in1(4'b1001), .out(multiplexer_14_out), .sel(div9));
  or or_3 (or_3_out, sbtype, MemRW);
  or or_4 (or_4_out, and_3_out, and_4_out, and_1_out, and_2_out, and_5_out);
  Multiplexer #(.width(4), .enable("false")) multiplexer_15 (
    .in0(multiplexer_14_out), .in1(4'b1010), .out(multiplexer_15_out), .sel(remu10));
  Comparator #(.width(7), .mode("unsigned")) comparator_14 (
    .a(in_2[6:0]), .b(7'b1100111), .eq(itype3));  // open: gt, lt
  not not_4 (RegWEn, or_3_out);
  or or_5 (or_5_out, utype1, utype2);
  Multiplexer #(.width(4), .enable("false")) multiplexer_16 (
    .in0(multiplexer_15_out), .in1(4'b1011), .out(multiplexer_16_out), .sel(srl11));
  Multiplexer #(.width(4), .enable("false")) multiplexer_17 (
    .in0(multiplexer_16_out), .in1(4'b1100), .out(multiplexer_17_out), .sel(sra12));
  Comparator #(.width(3), .mode("unsigned")) comparator_15 (
    .a(in_2[14:12]), .b(3'b110), .eq(comparator_15_eq));  // open: gt, lt
  and and_6 (and_6_out, or_4_out, sbtype);
  or or_6 (or_6_out, or_5_out, ujtype);
  Multiplexer #(.width(4), .enable("false")) multiplexer_18 (
    .in0(multiplexer_17_out), .in1(4'b1101), .out(multiplexer_18_out), .sel(slt13));
  or or_7 (or_7_out, comparator_15_eq, comparator_16_eq);
  Comparator #(.width(3), .mode("unsigned")) comparator_16 (
    .a(in_2[14:12]), .b(3'b111), .eq(comparator_16_eq));  // open: gt, lt
  or or_8 (PCSel, itype3, and_6_out, ujtype);
  Multiplexer #(.width(3), .enable("false")) multiplexer_19 (.in0(in_2[14:12]), .in1(3'b000), .out(f3), .sel(or_6_out));
  Multiplexer #(.width(4), .enable("false")) multiplexer_20 (
    .in0(multiplexer_18_out), .in1(4'b1110), .out(multiplexer_20_out), .sel(sll14));
  and and_7 (BrUn, or_7_out, sbtype);
  Multiplexer #(.width(4), .enable("false")) multiplexer_21 (
    .in0(4'b0000), .in1(multiplexer_20_out), .out(ALUSel), .sel(add0));
  Comparator #(.width(7), .mode("unsigned")) comparator_17 (
    .a(f7), .b({7{1'b0}}), .eq(comparator_17_eq));  // open: gt, lt
  Comparator #(.width(3), .mode("unsigned")) comparator_18 (.a(f3), .b(3'b111), .eq(comparator_18_eq));  // open: gt, lt
  or or_9 (add0, itype2, rtype);
  Comparator #(.width(7), .mode("unsigned")) comparator_19 (
    .a(f7), .b(7'b0000001), .eq(comparator_19_eq));  // open: gt, lt
  Comparator #(.width(3), .mode("unsigned")) comparator_20 (.a(f3), .b(3'b000), .eq(comparator_20_eq));  // open: gt, lt
  Comparator #(.width(7), .mode("unsigned")) comparator_21 (
    .a(f7), .b(7'b0000001), .eq(comparator_21_eq));  // open: gt, lt
  Comparator #(.width(3), .mode("unsigned")) comparator_22 (.a(f3), .b(3'b011), .eq(comparator_22_eq));  // open: gt, lt
  Comparator #(.width(7), .mode("unsigned")) comparator_23 (
    .a(f7), .b(7'b0000001), .eq(comparator_23_eq));  // open: gt, lt
  Comparator #(.width(3), .mode("unsigned")) comparator_24 (.a(f3), .b(3'b101), .eq(comparator_24_eq));  // open: gt, lt
  Comparator #(.width(7), .mode("unsigned")) comparator_25 (
    .a(f7), .b({7{1'b0}}), .eq(comparator_25_eq));  // open: gt, lt
  Comparator #(.width(3), .mode("unsigned")) comparator_26 (.a(f3), .b(3'b101), .eq(comparator_26_eq));  // open: gt, lt
  Comparator #(.width(7), .mode("unsigned")) comparator_27 (
    .a(f7), .b({7{1'b0}}), .eq(comparator_27_eq));  // open: gt, lt
  Comparator #(.width(3), .mode("unsigned")) comparator_28 (.a(f3), .b(3'b010), .eq(comparator_28_eq));  // open: gt, lt
  and and_8 (and3, comparator_17_eq, comparator_18_eq);
  and and_9 (mult5, comparator_19_eq, comparator_20_eq);
  and and_10 (mulhu6, comparator_21_eq, comparator_22_eq);
  and and_11 (divu8, comparator_23_eq, comparator_24_eq);
  and and_12 (srl11, comparator_25_eq, comparator_26_eq);
  and and_13 (slt13, comparator_27_eq, comparator_28_eq);
  Multiplexer #(.width(3), .enable("false")) multiplexer_22 (
    .in0(3'b000), .in1(3'b001), .out(multiplexer_22_out), .sel(MemRW));
  Comparator #(.width(3), .mode("unsigned")) comparator_29 (
    .a(in_2[14:12]), .b(3'b000), .eq(comparator_29_eq));  // open: gt, lt
  Multiplexer #(.width(3), .enable("false")) multiplexer_23 (
    .in0(multiplexer_22_out), .in1(3'b010), .out(multiplexer_23_out), .sel(sbtype));
  or or_10 (or_10_out, utype2, utype1);
  Comparator #(.width(7), .mode("unsigned")) comparator_30 (
    .a(f7), .b({7{1'b0}}), .eq(comparator_30_eq));  // open: gt, lt
  Comparator #(.width(3), .mode("unsigned")) comparator_31 (.a(f3), .b(3'b110), .eq(comparator_31_eq));  // open: gt, lt
  Comparator #(.width(7), .mode("unsigned")) comparator_32 (
    .a(f7), .b({7{1'b0}}), .eq(comparator_32_eq));  // open: gt, lt
  Comparator #(.width(3), .mode("unsigned")) comparator_33 (.a(f3), .b(3'b100), .eq(comparator_33_eq));  // open: gt, lt
  Comparator #(.width(7), .mode("unsigned")) comparator_34 (
    .a(f7), .b(7'b0000001), .eq(comparator_34_eq));  // open: gt, lt
  Comparator #(.width(3), .mode("unsigned")) comparator_35 (.a(f3), .b(3'b001), .eq(comparator_35_eq));  // open: gt, lt
  Comparator #(.width(7), .mode("unsigned")) comparator_36 (
    .a(f7), .b(7'b0000001), .eq(comparator_36_eq));  // open: gt, lt
  Comparator #(.width(3), .mode("unsigned")) comparator_37 (.a(f3), .b(3'b111), .eq(comparator_37_eq));  // open: gt, lt
  Comparator #(.width(7), .mode("unsigned")) comparator_38 (
    .a(f7), .b(7'b0100000), .eq(comparator_38_eq));  // open: gt, lt
  Comparator #(.width(3), .mode("unsigned")) comparator_39 (.a(f3), .b(3'b101), .eq(comparator_39_eq));  // open: gt, lt
  Multiplexer #(.width(3), .enable("false")) multiplexer_24 (
    .in0(3'b010), .in1(3'b000), .out(multiplexer_24_out), .sel(comparator_29_eq));
  Multiplexer #(.width(3), .enable("false")) multiplexer_25 (
    .in0(multiplexer_23_out), .in1(3'b011), .out(multiplexer_25_out), .sel(or_10_out));
  and and_14 (or1, comparator_30_eq, comparator_31_eq);
  and and_15 (xor2, comparator_32_eq, comparator_33_eq);
  Comparator #(.width(7), .mode("unsigned")) comparator_40 (
    .a(f7), .b(7'b0000001), .eq(comparator_40_eq));  // open: gt, lt
  Comparator #(.width(3), .mode("unsigned")) comparator_41 (.a(f3), .b(3'b100), .eq(comparator_41_eq));  // open: gt, lt
  Comparator #(.width(7), .mode("unsigned")) comparator_42 (
    .a(f7), .b({7{1'b0}}), .eq(comparator_42_eq));  // open: gt, lt
  Comparator #(.width(3), .mode("unsigned")) comparator_43 (.a(f3), .b(3'b001), .eq(comparator_43_eq));  // open: gt, lt
  Comparator #(.width(3), .mode("unsigned")) comparator_44 (
    .a(in_2[14:12]), .b(3'b001), .eq(comparator_44_eq));  // open: gt, lt
  Multiplexer #(.width(3), .enable("false")) multiplexer_26 (
    .in0(multiplexer_25_out), .in1(3'b100), .out(ImmSel), .sel(ujtype));
  and and_16 (div9, comparator_40_eq, comparator_41_eq);
  and and_17 (mulh7, comparator_34_eq, comparator_35_eq);
  and and_18 (remu10, comparator_36_eq, comparator_37_eq);
  and and_19 (sra12, comparator_38_eq, comparator_39_eq);
  and and_20 (sll14, comparator_42_eq, comparator_43_eq);
  Multiplexer #(.width(3), .enable("false")) multiplexer_27 (
    .in0(multiplexer_24_out), .in1(3'b001), .out(multiplexer_27_out), .sel(comparator_44_eq));
  Comparator #(.width(3), .mode("unsigned")) comparator_45 (
    .a(in_2[14:12]), .b(3'b010), .eq(comparator_45_eq));  // open: gt, lt
  Comparator #(.width(7), .mode("unsigned")) comparator_46 (
    .a(f7), .b(7'b0100000), .eq(comparator_46_eq));  // open: gt, lt
  Comparator #(.width(3), .mode("unsigned")) comparator_47 (.a(f3), .b(3'b000), .eq(comparator_47_eq));  // open: gt, lt
  Multiplexer #(.width(3), .enable("false")) multiplexer_28 (
    .in0(multiplexer_27_out), .in1(3'b010), .out(multiplexer_28_out), .sel(comparator_45_eq));
  Comparator #(.width(3), .mode("unsigned")) comparator_48 (
    .a(in_2[14:12]), .b(3'b100), .eq(comparator_48_eq));  // open: gt, lt
  and and_21 (sub4, comparator_46_eq, comparator_47_eq);
  Multiplexer #(.width(3), .enable("false")) multiplexer_29 (
    .in0(multiplexer_28_out), .in1(3'b011), .out(multiplexer_29_out), .sel(comparator_48_eq));
  Comparator #(.width(3), .mode("unsigned")) comparator_49 (
    .a(in_2[14:12]), .b(3'b101), .eq(comparator_49_eq));  // open: gt, lt
  Multiplexer #(.width(3), .enable("false")) multiplexer_30 (
    .in0(multiplexer_29_out), .in1(3'b100), .out(multiplexer_30_out), .sel(comparator_49_eq));
  Multiplexer #(.width(3), .enable("false")) multiplexer_31 (
    .in0(3'b010), .in1(multiplexer_30_out), .out(DataSel), .sel(itype1));

  // Other names for the same wires on the sheet: opcode[6:0] = in_2[6:0]; func3[2:0] = in_2[14:12];
  //   func7[6:0] = in_2[31:25]; stype = MemRW
endmodule
